# Fritzing sketch PCB ITsat v2 (saved by Fritzing 0.9.2b)
circuit board: 5.6cm x 5.6cm
breadboards: 1

parts:
  ITsat = Arduino Nano (Rev3.0)
  J1 = female pin header, 1 pin [form="♀ (female)"]
  VCC1 = Battery
  J2 = female pin header, 1 pin [form="♀ (female)"]
  MQ-4 = female pin header, 3 pins [form="♀ (female)"]
  GPS = female pin header, 4 pins [form="♀ (female)"]
  Camara = female pin header, 2 pins [form="♀ (female)"]
  Buzzer = female pin header, 2 pins [form="♀ (female)"]
  Led = female pin header, 2 pins [form="♀ (female)"]
  J3 = female pin header, 4 pins [form="♀ (female)"]
  Parte1 = OpenLog
  J4 = female pin header, 4 pins [form="♀ (female)"]

nets:
  N1: ITsat.D1/TX, J3.pin1, Parte1.RXI
  N2: ITsat.D0/RX, J3.pin2, Parte1.TXO
  N3: ITsat.D3, GPS.pin2
  N4: ITsat.D4, GPS.pin3
  N5: ITsat.VIN, J1.pin1
  5V: ITsat.5V, MQ-4.pin3, GPS.pin4, Camara.pin1, Buzzer.pin2, Led.pin1, J3.pin3, Parte1.VCC, J4.pin1
  N6: ITsat.A5, J4.pin3
  N7: ITsat.A4, J4.pin2
  N8: ITsat.A0, MQ-4.pin1
  N9: VCC1.+, J2.pin1
